// Logisim project d_flipflop_async.circ as structural Verilog
module main (
  input  CLR,
  input  D,
  input  SET,
  input  CLK,
  output Q,
  output not_Q
);

  wire and_1_out, and_2_out, and_3_out, and_4_out, nor_1_out, nor_2_out, not_1_out, not_2_out;

  not not_1 (not_1_out, D);
  and and_1 (and_1_out, D, CLK);
  and and_2 (and_2_out, CLK, not_1_out);
  not not_2 (not_2_out, CLK);
  nor nor_1 (nor_1_out, and_1_out, nor_2_out);
  nor nor_2 (nor_2_out, nor_1_out, and_2_out);
  and and_3 (and_3_out, not_2_out, nor_1_out);
  and and_4 (and_4_out, nor_2_out, not_2_out);
  nor nor_3 (Q, CLR, and_3_out, not_Q);
  nor nor_4 (not_Q, Q, and_4_out, SET);
endmodule

// VHDL entity D_FF_ASYNC, as the project stores it:
library IEEE;
use IEEE.STD_LOGIC_1164.ALL;

entity D_FF_ASYNC is
    Port (
        D   : in  STD_LOGIC;
        clk : in  STD_LOGIC;
        set : in  STD_LOGIC;
        clr : in  STD_LOGIC;
        Q   : out STD_LOGIC;
        Qn  : out STD_LOGIC
    );
end D_FF_ASYNC;

architecture Behavioral of D_FF_ASYNC is
    signal q_int : STD_LOGIC := '0';
begin

    process(clk, set, clr)
    begin
        if clr = '1' then
            q_int <= '0';

        elsif set = '1' then
            q_int <= '1';

        elsif rising_edge(clk) then
            q_int <= D;
        end if;
    end process;

    Q  <= q_int;
    Qn <= not q_int;

end Behavioral;
